# Fritzing sketch eFingerJointJig (saved by Fritzing 0.9.3b)
circuit board: 22.4674cm x 3.65407cm
breadboards: 1

parts:
  Composant1 = Arduino Nano (Rev3.0)
  VCC1 = Battery block 9V
  S1 = Taiway 100-SP-X-T1 SPDT Miniature Toggle Switch [part_number=100-SP-X-T1-0-0-B1-M1 package=THT]
  Grove1 = Grove Infrared Receiver
  Grove2 = Grove Infrared Receiver
  LED1 = LED - 5mm [color="Red (633nm)" package="5 mm [THT]"]
  LED2 = smd LED [color="Red (633nm)" package="0805 [SMD]"]
  LED3 = smd LED [color="Red (633nm)" package="0805 [SMD]"]
  LED4 = LED - 5mm [color="Green (555nm)" package="5 mm [THT]"]
  LED5 = LED - 5mm [color="Green (555nm)" package="5 mm [THT]"]
  LED6 = LED - 5mm [color="Green (555nm)" package="5 mm [THT]"]
  LED7 = LED - 5mm [color="Green (555nm)" package="5 mm [THT]"]
  LED8 = LED - 5mm [color="Green (555nm)" package="5 mm [THT]"]
  LED9 = LED - 5mm [color="Green (555nm)" package="5 mm [THT]"]
  LED10 = LED - 5mm [color="Green (555nm)" package="5 mm [THT]"]
  LED11 = LED - 5mm [color="Green (555nm)" package="5 mm [THT]"]
  switch1 = Rotary_Switch_12x1
  R12 = Resistor [tolerance=±5% resistance=1k package=THT]
  R13 = Resistor [tolerance=±5% resistance=1k package=THT]
  R14 = Resistor [tolerance=±5% resistance=1k package=THT]
  R15 = Resistor [tolerance=±5% resistance=1k package=THT]
  R16 = Resistor [tolerance=±5% resistance=1k package=THT]
  R17 = Resistor [tolerance=±5% resistance=1k package=THT]
  R11 = Resistor [tolerance=±5% resistance=330 package=THT]
  R10 = Resistor [tolerance=±5% resistance=330 package=THT]
  R9 = Resistor [tolerance=±5% resistance=330 package=THT]
  R8 = Resistor [tolerance=±5% resistance=330 package="2512 [SMD]"]
  R7 = Resistor [tolerance=±5% resistance=330 package=THT]
  R6 = Resistor [tolerance=±5% resistance=330 package=THT]
  R5 = Resistor [tolerance=±5% resistance=330 package=THT]
  R4 = Resistor [tolerance=±5% resistance=330 package=THT]
  R3 = Resistor [tolerance=±5% resistance=330 package=THT]
  R2 = Resistor [tolerance=±5% resistance=330 package=THT]
  R1 = Resistor [tolerance=±5% resistance=330 package=THT]

nets:
  GND: Composant1.GND, VCC1.-, Grove1.GND, Grove2.GND, switch1.2, switch1.3, switch1.4, switch1.5, switch1.6, R12.Pin_1, R10.Pin_0, R9.Pin_0, R7.Pin_0, R6.Pin_0, R4.Pin_0, R3.Pin_0, R1.Pin_0
  N1: Composant1.D2, Grove1.RX
  N2: Composant1.D3, Grove2.RX
  N3: Composant1.D4, LED7.anode
  N4: Composant1.D5, LED6.anode
  N5: Composant1.D6, LED5.anode
  N6: Composant1.D7, LED4.anode
  N7: Composant1.D8, LED3.anode
  N8: Composant1.D9, LED2.anode
  N9: Composant1.D10, LED1.anode
  N10: Composant1.D11/MOSI, LED8.anode
  N11: Composant1.D12/MISO, LED9.anode
  N12: Composant1.VIN, S1.L2
  VCC: Composant1.5V, Grove1.VCC, Grove2.VCC
  N13: Composant1.A3, LED11.anode
  N14: Composant1.A2, LED10.anode
  N15: Composant1.A1, switch1.0
  N16: Composant1.D13/SCK, switch1.1, R17.Pin_0
  N17: VCC1.+, S1.COM
  N18: LED1.cathode, R5.Pin_1
  N19: LED2.cathode, R6.Pin_1
  N20: LED3.cathode, R7.Pin_1
  N21: LED4.cathode, R8.Pin_1
  N22: LED5.cathode, R9.Pin_1
  N23: LED6.cathode, R10.Pin_1
  N24: LED7.cathode, R11.Pin_1
  N25: LED8.cathode, R4.Pin_1
  N26: LED9.cathode, R3.Pin_1
  N27: LED10.cathode, R2.Pin_1
  N28: LED11.cathode, R1.Pin_1
  N29: switch1.7, switch1.8, R12.Pin_0, R13.Pin_0, R13.Pin_1, R14.Pin_0
  N30: switch1.9, R14.Pin_1, R15.Pin_0
  N31: switch1.10, R15.Pin_1, R16.Pin_0
  N32: switch1.11, switch1.12, R16.Pin_1, R17.Pin_1
